# Fritzing sketch Play music with arduino (saved by Fritzing 0.9.3b)
breadboards: 1

parts:
  Componente1 = Arduino Uno (Rev3)
  LCD1 = LCD screen
  R2 = Resistor [tolerance=±5% resistance=220 package="2512 [SMD]"]
  IR1 = TSOP312.., 314.. [package=THT]
  J1 = Piezo Speaker
  R3 = Trimmer Potentiometer [maximum_resistance=10kΩ package=THT]
  R4 = Resistor [tolerance=±5% resistance=220 package=THT]

nets:
  N1: Componente1.D8, LCD1.E
  N2: Componente1.D9_PWM, LCD1.RS
  N3: Componente1.D11_PWM/MOSI, R4.Pin_1
  GND: Componente1.GND, LCD1.VSS, LCD1.R/W, LCD1.LED-, IR1.GND, J1.pin1, R3.leg1
  N4: Componente1.D2, IR1.Data
  N5: Componente1.D4, LCD1.DB7
  N6: Componente1.D5_PWM, LCD1.DB6
  N7: Componente1.D6_PWM, LCD1.DB5
  N8: Componente1.D7, LCD1.DB4
  5V: Componente1.5V, LCD1.VDD, R2.Pin_0, IR1.Vs, R3.leg2
  N9: LCD1.V0, R3.wiper
  N10: LCD1.LED+, R2.Pin_1

// code stored in the sketch: Fritzing Monitor Tastiera Arduino.ino
#include <Keypad.h>
#include <LiquidCrystal.h>
#include <avr/io.h>
#include <avr/wdt.h>

#define Reset_AVR() wdt_enable(WDTO_30MS); while(1) {} 

#define BUZZ 13             

const byte ROWS = 2;
const byte COLS = 3;
char hexaKeys[ROWS][COLS] = {
  {'1','2','3'},
  {'4','5','6'}
};
byte rowPins[ROWS] = {12, 11};
byte colPins[COLS] = {10, 9, 8};

Keypad customKeypad = Keypad( makeKeymap(hexaKeys), rowPins, colPins, ROWS, COLS); 

LiquidCrystal lcd(7, 6, 5, 4, 3, 2);
  
void setup() {                  
  lcd.begin(16,2);
  lcd.setCursor(0,0);
  lcd.print("--Selezionare--");
  lcd.setCursor(0,1);
  lcd.print("----Canzone----");
  pinMode(BUZZ, OUTPUT);
  Serial.begin(9600);
}  

void loop() {
  char customKey = customKeypad.getKey();
  if (customKey=='1') {  
    lcd.clear();
    lcd.setCursor(0,0);
    lcd.print("Inno alla Gioia");    
    delay(2000);
    nota_mi();
    nota_mi();
    nota_fa();
    nota_sol();         
    nota_sol();
    nota_fa();
    nota_mi();
    nota_re();    
    nota_do();
    nota_do();
    nota_re();
    nota_mi();          
    nota_misemmin();
    nota_recroma();
    nota_reminima();             
    nota_mi();               
    nota_mi();
    nota_fa();
    nota_sol();
    nota_sol();
    nota_fa();
    nota_mi();
    nota_re();
    nota_do();
    nota_do();
    nota_re();
    nota_mi();
    nota_resemmin();
    nota_docroma();
    nota_dominima();
    nota_re();
    nota_re();
    nota_mi();
    nota_do();
    nota_re();
    nota_microma();
    nota_facroma();
    nota_mi();
    nota_do();
    nota_re();
    nota_microma();
    nota_facroma();
    nota_mi();
    nota_re();
    nota_do();
    nota_re();
    nota_solminima();
    nota_mi();               
    nota_mi();
    nota_fa();
    nota_sol();
    nota_sol();
    nota_fa();
    nota_mi();
    nota_re();
    nota_do();
    nota_do();
    nota_re();
    nota_mi();
    nota_resemmin();
    nota_docroma();
    nota_dominima();
    lcd.clear();
    delay(100);  
    Reset_AVR();
  }
  
  else if (customKey=='2') {  
    lcd.clear();
    lcd.setCursor(0,0);
    lcd.print("London Bridge");
    lcd.setCursor(0,1);
    lcd.print("Is falling down");  
    delay(2000);
    nota_solsemmin();
    nota_lacroma();
    nota_sol();
    nota_fa();
    nota_mi();
    nota_fa();
    nota_solminima();
    nota_re();
    nota_mi();
    nota_faminima();
    nota_mi();
    nota_fa();
    nota_solminima();
    nota_solsemmin();
    nota_lacroma();
    nota_sol();
    nota_fa();
    nota_mi();
    nota_fa();
    nota_solminima();
    nota_reminima();
    nota_solminima();
    nota_mi();
    nota_dosemmin();
    lcd.clear();
    delay(100);
    Reset_AVR();
  }
  else if (customKey=='3') {  
    lcd.clear();
    lcd.setCursor(0,0);
    lcd.print("Fur Elise");
    delay(2000);
    nota_microma();
    nota_recroma();
    nota_microma();
    nota_recroma();
    nota_microma();
    nota_sicroma();
    nota_recroma();
    nota_docroma();
    nota_lasemmin();
    nota_docroma();
    nota_microma();
    nota_lacroma();
    nota_sisemmin();
    nota_microma();
    nota_solcroma();
    nota_sicroma();
    nota_dosemmin();
    nota_microma();
    nota_microma();
    nota_recroma();
    nota_microma();
    nota_recroma();
    nota_microma();
    nota_sicroma();
    nota_recroma();
    nota_docroma();
    nota_lasemmin();
    nota_docroma();
    nota_microma();
    nota_lacroma();
    nota_solsemmin();
    nota_microma();
    nota_docroma();
    nota_sicroma();
    nota_laminima();
    nota_microma();
    nota_recroma();
    nota_microma();
    nota_recroma();
    nota_microma();
    nota_sicroma();
    nota_recroma();
    nota_docroma();
    nota_lasemmin();
    nota_docroma();
    nota_microma();
    nota_lacroma();
    nota_sisemmin();
    nota_microma();
    nota_solcroma();
    nota_sicroma();
    nota_dosemmin();
    lcd.clear();
    delay(100);
    Reset_AVR();
  }
} 

void nota_dosemcr() {
  lcd.clear();
  lcd.setCursor(0, 0);
  lcd.print("Do Minima");
  tone(13,262,75); //DO
  delay(100);
  }
void nota_docroma() {
  lcd.clear();
  lcd.setCursor(0, 0);
  lcd.print("Do Croma");
  tone(13,262,150); //DO
  delay(200);
  }
void nota_do() {
  lcd.clear();
  lcd.setCursor(0, 0);
  lcd.print("Do Semiminima");
  tone(13,262,300); //DO
  delay(400);
  }
void nota_dosemmin() {
  lcd.clear();
  lcd.setCursor(0, 0);
  lcd.print("Do Semiminima +");
  lcd.setCursor(0,1);
  lcd.print("   Croma");
  tone(13,262,450); //DO
  delay(600);
  }
void nota_dominima() {
  lcd.clear();
  lcd.setCursor(0, 0);
  lcd.print("Do Minima");
  tone(13,262,600); //DO
  delay(800);
  }
void nota_dominsem() {
  lcd.clear();
  lcd.setCursor(0, 0);
  lcd.print("Do Minima +");
  lcd.setCursor(0,1);
  lcd.print("   Semiminima");
  tone(13,262,900); //DO
  delay(1200);
  }

void nota_resemcr() {
  lcd.clear();
  lcd.setCursor(0, 0);
  lcd.print("Re Semicroma");
  tone(13,294,75); //RE
  delay(100);
  }
void nota_recroma() {
  lcd.clear();
  lcd.setCursor(0, 0);
  lcd.print("Re Croma");
  tone(13,294,150); //RE
  delay(200);
  }
void nota_re() {
  lcd.clear();
  lcd.setCursor(0, 0);
  lcd.print("Re Semiminima");
  tone(13,294,300); //RE
  delay(400);
  }
void nota_resemmin() {
  lcd.clear();
  lcd.setCursor(0, 0);
  lcd.print("Re Semiminima +");
  lcd.setCursor(0,1);
  lcd.print("   Croma");
  tone(13,294,450);
  delay(600);
  }
void nota_reminima() {
  lcd.clear();
  lcd.setCursor(0, 0);
  lcd.print("Re Minima");
  tone(13,294,600); //RE
  delay(800);
  }
void nota_reeee() {
  lcd.clear();
  lcd.setCursor(0, 0);
  lcd.print("Re Semibreve");
  tone(13,294,1200); //RE
  delay(1600);
  }

void nota_misemcr() {
  lcd.clear();
  lcd.setCursor(0, 0);
  lcd.print("Mi Semicroma");
  tone(13,330,75); //MI
  delay(100);
  }
void nota_microma() {
  lcd.clear();
  lcd.setCursor(0, 0);
  lcd.print("Mi Croma");
  tone(13,330,150); //MI
  delay(200);
  }
void nota_mi() {
  lcd.clear();
  lcd.setCursor(0, 0);
  lcd.print("Mi Semiminima");
  tone(13,330,300); //MI
  delay(400);
  }
void nota_misemmin() {
  lcd.clear();
  lcd.setCursor(0, 0);
  lcd.print("Mi Semiminima +");
  lcd.setCursor(0,1);
  lcd.print("   Croma");
  tone(13,330,450); //MI
  delay(600);
  }
void nota_faaaa() {
  lcd.clear();
  lcd.setCursor(0, 0);
  lcd.print("Fa Semibreve");
  tone(13,349,1200); //FA
  delay(1600);
  }

void nota_facroma() {
  lcd.clear();
  lcd.setCursor(0, 0);
  lcd.print("Fa Croma");
  tone(13,349,150); //FA
  delay(200);
  }
void nota_fa() {
  lcd.clear();
  lcd.setCursor(0, 0);
  lcd.print("Fa Semiminima");
  tone(13,349,300); //FA
  delay(400);
  }
void nota_fasemmin() {
  lcd.clear();
  lcd.setCursor(0, 0);
  lcd.print("Fa Semiminima +");
  lcd.setCursor(0,1);
  lcd.print("   Croma");
  tone(13,349,450); //FA
  delay(600);
  }
void nota_faminima() {
  lcd.clear();
  lcd.setCursor(0, 0);
  lcd.print("Fa Minima");
  tone(13,349,600); //FA
  delay(800);
  }

void nota_solcroma() {
  lcd.clear();
  lcd.setCursor(0, 0);
  lcd.print("Sol Croma");
  tone(13,392,150); //SOL
  delay(200);
  }
void nota_sol() {
  lcd.clear();
  lcd.setCursor(0, 0);
  lcd.print("Sol Semiminima");
  tone(13,392,300); //SOL
  delay(400);
  }
void nota_solsemmin() {
  lcd.clear();
  lcd.setCursor(0, 0);
  lcd.print("Sol Semiminima +");
  lcd.setCursor(0,1);
  lcd.print("   Croma");
  tone(13,392,450); 
  delay(600);
  }
void nota_solminima() {
  lcd.clear();
  lcd.setCursor(0, 0);
  lcd.print("Sol Minima");
  tone(13,392,600); //SOL
  delay(800);
  }

void nota_lasemcr() {
  lcd.clear();
  lcd.setCursor(0, 0);
  lcd.print("La Semicroma");
  tone(13,430,75); //LA
  delay(100);
  }
void nota_lacroma() {
  lcd.clear();
  lcd.setCursor(0, 0);
  lcd.print("La Croma");
  tone(13,430,150); //LA
  delay(200);
  }
void nota_la() {
  lcd.clear();
  lcd.setCursor(0, 0);
  lcd.print("La Semiminima");
  tone(13,430,300); //LA
  delay(400);
  } 
void nota_lasemmin() {
  lcd.clear();
  lcd.setCursor(0, 0);
  lcd.print("La Semiminima +");
  lcd.setCursor(0,1);
  lcd.print("   Croma");
  tone(13,430,450); //LA
  delay(600);
  }
void nota_laminima() {
  lcd.clear();
  lcd.setCursor(0, 0);
  lcd.print("La Minima");
  tone(13,430,600); //LA
  delay(800);
  } 

void nota_sisemcr() {
  lcd.clear();
  lcd.setCursor(0, 0);
  lcd.print("Si Semicroma");
  tone(13,462,75); //SI
  delay(100);
  }
void nota_sicroma() {
  lcd.clear();
  lcd.setCursor(0, 0);
  lcd.print("Si Croma");
  tone(13,462,150); //SI
  delay(200);
  }
void nota_si() {
  lcd.clear();
  lcd.setCursor(0, 0);
  lcd.print("Si Semiminima");
  tone(13,462,300); //SI
  delay(400);
  }
void nota_sisemmin() {
  lcd.clear();
  lcd.setCursor(0, 0);
  lcd.print("Si Semiminima +");
  lcd.setCursor(0,1);
  lcd.print("   Croma");
  tone(13,462,450); //SI
  delay(600);
  }
